# Fritzing sketch domohome_v1_breadboard (saved by Fritzing 0.9.3b)

parts:
  Raspberry_Pi1 = Raspberry Pi 2
  KY-2 = Keyes Relay [package=THT]
  KY-3 = Keyes Relay [package=THT]
  DHT22 = DHT22 Humidity and Temperature Sensor
  Foto_relé = S1133 Si Photodiode [package="8mm Ceramic [THT]"]

nets:
  3V3: Raspberry_Pi1.3v3, DHT22.VDD
  N1: Raspberry_Pi1.GPIO4, DHT22.DATA
  GND: Raspberry_Pi1.GND, KY-2.ground, KY-3.ground, DHT22.GND, Foto_relé.anode
  N2: Raspberry_Pi1.GPIO5, Foto_relé.cathode
  N3: Raspberry_Pi1.GPIO6, KY-3.power
  N4: Raspberry_Pi1.GPIO19, KY-2.power
  N5: Raspberry_Pi1.5V, KY-2.signal, KY-3.signal

custom parts:
  Keyes Relay: The Keyes 5V relay module is suitable for SCM development, home appliance control. It uses a 5V~12V TIL control signal which can control DC / AC signal.
